# Fritzing sketch ProgettoIenius (saved by Fritzing 0.9.3b)
breadboards: 3

parts:
  Componente1 = Arduino Mega 2560 (Rev3)
  Componente2 = Bluetooth HC-05 Macho
  S3 = Pushbutton [package="[THT]"]
  S4 = Pushbutton [package="[THT]"]
  U1 = MAX6675 [package=so08]
  F1 = Fan - Ventilador [package=THT]
  VCC1 = Battery block 9V
  LED4 = LED - 5mm [color="Red (633nm)" package="5 mm [THT]"]
  LED5 = LED - 5mm [color="Green (565nm)" package="5 mm [THT]"]
  LED6 = LED - 5mm [color="Blue (470nm)" package="5 mm [THT]"]
  R1 = Resistor [tolerance=±5% resistance=220 package="0805 [SMD]"]
  R2 = Resistor [tolerance=±5% resistance=220 package="0805 [SMD]"]
  R3 = Resistor [tolerance=±5% resistance=220 package="0805 [SMD]"]
  R4 = Resistor [tolerance=±5% resistance=220 package="0805 [SMD]"]
  R5 = Resistor [tolerance=±5% resistance=220 package="0805 [SMD]"]
  OMRON2 = OMRON PCB Power Relay – G5LE [part_number="G5LE-1\n" package=THT]
  OMRON3 = OMRON PCB Power Relay – G5LE [part_number="G5LE-1\n" package=THT]
  OMRON4 = OMRON PCB Power Relay – G5LE [part_number="G5LE-1\n" package=THT]
  OMRON5 = OMRON PCB Power Relay – G5LE [part_number="G5LE-1\n" package=THT]
  OMRON1 = OMRON PCB Power Relay – G5LE [part_number="G5LE-1\n" package=THT]
  U2 = BUTTON-MAGNETIC [package=Magnetic-snap]
  U3 = BUTTON-MAGNETIC [package=Magnetic-snap]
  J1 = Piezo Speaker
  LED7 = LED - 5mm [color="Red (633nm)" package="5 mm [THT]"]
  J2 = Piezo Speaker

nets:
  N1: Componente1.D21/SCL, S4.Pin_3, S4.Pin_4, R5.Pin_0
  N2: Componente1.D20/SDA, S3.Pin_3, S3.Pin_4, R4.Pin_0
  N3: Componente1.D11_PWM, Componente2.TXD
  N4: Componente1.D10_PWM, Componente2.RXD
  5V: Componente1.5V, Componente2.VCC, S3.Pin_1, S3.Pin_2, S4.Pin_1, S4.Pin_2
  GND: Componente1.GND, Componente2.GND, F1.GND, LED4.cathode, LED5.cathode, LED6.cathode, R4.Pin_1, R5.Pin_1, OMRON2.COIL1, OMRON3.COIL1, OMRON4.COIL1, OMRON5.COIL1, OMRON1.COIL1, J1.pin1, LED7.cathode, J2.pin1
  N5: Componente1.D5_PWM, U1.SCK
  N6: Componente1.D6_PWM, U1.CS
  N7: Componente1.D7_PWM, U1.MISO
  N8: Componente1.D32, R2.Pin_0
  N9: Componente1.D33, F1.5V
  N10: Componente1.D34, R3.Pin_0
  N11: Componente1.D35, OMRON2.COIL2
  N12: Componente1.D36, R1.Pin_0
  N13: Componente1.D37, OMRON3.COIL2
  N14: Componente1.D40, OMRON1.COIL2
  N15: Componente1.D41, OMRON4.COIL2
  N16: Componente1.D42, OMRON5.COIL2
  N17: VCC1.+, OMRON2.C, OMRON3.C, OMRON4.C, OMRON5.C, OMRON1.C
  N18: LED4.anode, R2.Pin_1
  N19: LED5.anode, R3.Pin_1
  N20: LED6.anode, R1.Pin_1
  N21: OMRON2.B, U3.1
  N22: OMRON3.B, U2.1
  N23: OMRON4.B, J1.pin2
  N24: OMRON5.B, LED7.anode
  N25: OMRON1.B, J2.pin2

custom parts:
  Fan - Ventilador: Ventilador de 2 pines, se encuentra comunmente en computadoras de escritorio
